// Logisim project procesor.circ as structural Verilog
module Procesor (
  input  [15:0] in_1,
  input  LD,
  input  in_3,
  input  [15:0] in_4,
  input  LD_2,
  output [15:0] out_6,
  output [7:0] out_7,
  output [7:0] out_8,
  output [7:0] out_9,
  output [7:0] out_10
);

  wire clk, main_1_p3, main_1_p4, main_1_p5, main_1_p6, main_1_p7, registers_1_p7, registers_1_p8;

  Clock u_CLK (.out(clk));
  // CU_main main_1: pin names not known; wires that end beside it: in_4, out_9, main_1_p3, main_1_p4, main_1_p5, main_1_p6, main_1_p7
  RAM #(.dataWidth(16), .bus("separate")) ram_1 (
    .din(in_1), .data(out_6), .clk(clk), .ld(LD));  // open: addr, str, sel, clr
  // Registers registers_1: pin names not known; wires that end beside it: out_10, main_1_p5, main_1_p7, main_1_p6, clk, in_3, registers_1_p7, registers_1_p8, out_8
  RAM #(.bus("separate")) ram_2 (.addr(out_9), .data(out_10), .clk(clk), .ld(LD_2));  // open: din, str, sel, clr
  // ALU alu_1: pin names not known; wires that end beside it: out_8, registers_1_p7, registers_1_p8, main_1_p4, out_7

  // Other names for the same wires on the sheet: MEM[7:0] = out_9

  // Notes on the sheet:
  //   INSTRUCTIONS
  //   DATA
endmodule
